// Logisim project CdM-8-WOR-2016-grobot-V2.circ as structural Verilog: 28 circuits, main circuit system board
// CdM8
module CdM_8 (
  input  clk,
  input  rset,
  input  [7:0] data_in,
  input  IRQ,
  input  [2:0] vector,
  output data_code_prime,
  output [7:0] R0,
  output [7:0] R1,
  output mem,
  output [7:0] R2,
  output load_st_prime,
  output [7:0] R3,
  output [7:0] PC,
  output [7:0] addr,
  output [7:0] SP,
  output [7:0] data_out,
  output [2:0] page,
  output IAck
);

  wire _1cycle, alu_b, alu_u, alu_u1, and_1_out, and_2_out, and_5_out, and_6_out, and_7_out, and_8_out,
       and_10_out, and_13_out, and_16_out, and_17_out, and_20_out, and_21_out, and_22_out, and_23_out,
       br_dcsn_1_go, branch, Cl, cmp, crc, Fetch, HALT_prime, ioi, jsr, L_CVZN, L_Pg, Latch, latchPC,
       LatchPSR, ldc, ldi, ldi_plus, ldsp, mem_op, nand_1_out, nor_1_out, not_1_out, not_5_out, not_6_out,
       odd, or_1_out, or_2_out, or_3_out, or_5_out, or_6_out, or_7_out, osi, osix, PC2b0, PC2b1, PCinc, Ph1,
       Ph2, Ph3, Ph4, Ph5, po, PSR2b1, pu, Rd_as_src, RdA, RRA, rs_latch_2_q_prime, rs_latch_3_q_prime, RsA,
       rti, rts, RX2pc, RXL, SP2b0, SP2b1, SPact, SPL, stsp, up_dwn_prime, vec, WAIT;
  wire [0:0] decoder_2x4_5_out;
  wire [2:0] fun_b, n3mux2x1_1_out, n3mux2x1_2_out, PgReg, phase_cntr_1_phase, register_1_q;
  wire [2:2] not_2_out, rs_latch_1_q;
  wire [3:0] alu_1_cvzn, cccc, CVZN, decoder_2x4_7_out, PrSt;
  wire [3:1] decoder_2x4_3_out, vec_adr;
  wire [3:2] decoder_2x4_1_out;
  wire [7:0] alu_1_r, n8demux1x2_1_out0, regfile_1_bus0o;
  wire [7:7] Instr;

  or or_1 (or_1_out, IAck, rset);
  and and_1 (and_1_out, WAIT, Ph1, Cl);
  Pull_Resistor pull_resistor_1 (.node(RsA));
  Pull_Resistor pull_resistor_2 (.node(Rd_as_src));
  Pull_Resistor pull_resistor_3 (.node(latchPC));
  Pull_Resistor pull_resistor_4 (.node(PCinc));
  Pull_Resistor pull_resistor_5 (.node(PC2b1));
  Pull_Resistor pull_resistor_6 (.node(PC2b0));
  and and_2 (and_2_out, Fetch, ~Cl);  // AND_Gate
  RS_latch rs_latch_1 (.S(IAck), .R(or_5_out), .Q(rs_latch_1_q[2]));  // open: Q_prime
  and and_3 (Cl, clk, HALT_prime, nand_1_out);
  nand nand_1 (nand_1_out, rs_latch_2_q_prime, Fetch);
  RS_latch rs_latch_2 (.S(or_1_out), .R(and_1_out), .Q_prime(rs_latch_2_q_prime));  // open: Q
  Pull_Resistor pull_resistor_7 (.node(Latch));
  Pull_Resistor pull_resistor_8 (.node(RdA));
  Pull_Resistor pull_resistor_9 (.node(L_Pg));
  RS_latch rs_latch_3 (.S(L_Pg), .R(or_2_out), .Q_prime(rs_latch_3_q_prime));  // open: Q
  or or_2 (or_2_out, and_2_out, rset);
  not not_1 (not_1_out, phase_cntr_1_phase[2]);
  phase_cntr phase_cntr_1 (.phase(phase_cntr_1_phase), .restart(or_3_out), .Cl(Cl), .Reset(rset), .hold(1'b0));
  or or_3 (or_3_out, and_5_out, and_6_out, Ph5);
  or or_4 (_1cycle, WAIT, po, ldi, rts, alu_u, mem_op, ldsp, stsp, branch, cmp);
  or or_5 (or_5_out, and_7_out, rset);
  assign vec_adr = {3{rs_latch_1_q[2]}} & register_1_q;  // AND_Gate and_4, 3 bits wide
  _8demux1x2 u_8demux1x2_1 (.in(alu_1_r), .sel(alu_u1), .out1(data_in), .out0(n8demux1x2_1_out0));
  decoder_2x4 decoder_2x4_1 (
    .in(phase_cntr_1_phase[1:0]), .en(phase_cntr_1_phase[2]), .out({decoder_2x4_1_out, Ph5, Ph4}));
  decoder_2x4 decoder_2x4_2 (.in(phase_cntr_1_phase[1:0]), .en(not_1_out), .out({Ph3, Ph2, Ph1, Fetch}));
  and and_5 (and_5_out, Ph1, _1cycle);
  and and_6 (and_6_out, Ph2, ~or_6_out);  // AND_Gate
  and and_7 (and_7_out, Fetch, ~and_8_out);  // AND_Gate
  RS_latch rs_latch_4 (.S(and_8_out), .R(or_7_out), .Q(IAck));  // open: Q_prime
  Pull_Resistor pull_resistor_10 (.node(odd));
  Pull_Resistor pull_resistor_11 (.node(RRA));
  Pull_Resistor pull_resistor_12 (.node(RXL));
  Pull_Resistor pull_resistor_13 (.node(RX2pc));
  not not_2 (not_2_out[2], ioi);
  _3mux2x1 u_3mux2x1_1 (.in0(PgReg), .select(rs_latch_3_q_prime), .in1(PrSt[2:0]), .out(n3mux2x1_1_out));
  or or_6 (or_6_out, osix, ioi);
  and and_8 (and_8_out, PrSt[3], IRQ, Fetch);
  or or_7 (or_7_out, nor_1_out, rset);
  assign page = {3{not_2_out[2]}} & n3mux2x1_1_out;  // AND_Gate and_9, 3 bits wide
  buf buffer_1 (PC2b0, and_10_out);
  buf buffer_2 (PCinc, and_10_out);
  buf buffer_3 (mem, and_10_out);
  buf buffer_4 (load_st_prime, and_10_out);
  and and_10 (and_10_out, Fetch, ~IAck);  // AND_Gate
  nor nor_1 (nor_1_out, Cl, IRQ);
  Register #(.width(3)) register_1 (.D(vector), .en(and_8_out), .Q(register_1_q), .clk(Cl), .clr(rset));
  regfile regfile_1 (
    .RsSel(cccc[3:2]), .RsAssert(RsA), .UseRd_Rs_prime(Rd_as_src), .RdSel(cccc[1:0]), .RdAssert(RdA),
    .latch(Latch), .Bus1(data_in), .ALUres(n8demux1x2_1_out0), .Bus0o(regfile_1_bus0o), .Bus1o(data_in),
    .Cl(Cl), .rset(rset), .RR2bus1(RRA), .latchRX(RXL), .rx2pc_b12pc_prime(RX2pc), .latchPC(latchPC),
    .PCinc(PCinc), .PC2bus1(PC2b1), .PC2bus0(PC2b0), .up_down_prime(up_dwn_prime), .latchSP(SPL),
    .SPact(SPact), .SP2bus1(SP2b1), .SP2bus0(SP2b0), .R0(R0), .R1(R1), .R2(R2), .R3(R3), .PC(PC), .SP(SP));
  Pull_Resistor pull_resistor_14 (.node(up_dwn_prime));
  Pull_Resistor pull_resistor_15 (.node(SPact));
  Pull_Resistor pull_resistor_16 (.node(SPL));
  Pull_Resistor pull_resistor_17 (.node(vec));
  Pull_Resistor pull_resistor_18 (.node(SP2b1));
  Pull_Resistor pull_resistor_19 (.node(SP2b0));
  // Probe on {Instr[7], fun_b, cccc}
  Pull_Resistor pull_resistor_20 (.node(IRQ));
  Pull_Resistor pull_resistor_21 (.node(data_code_prime));
  Pull_Resistor pull_resistor_22 (.node(load_st_prime));
  _8mux2x1 u_8mux2x1_1 (.in0(regfile_1_bus0o), .select(vec), .in1({4'b1111, vec_adr, odd}), .out(addr));
  _3mux2x1 u_3mux2x1_2 (.in0(fun_b), .select(alu_u), .in1({fun_b[0], cccc[3:2]}), .out(n3mux2x1_2_out));
  Pull_Resistor pull_resistor_23 (.node(mem));
  // Probe on data_in
  ALU alu_1 (
    .fun(n3mux2x1_2_out), .u_b_prime(alu_u), .X(regfile_1_bus0o), .Y(data_in), .CVZN(alu_1_cvzn),
    .R(alu_1_r), .C(CVZN[3]));
  // Probe on CVZN[3]
  and and_11 (ldi_plus, Instr[7], fun_b[2], ~fun_b[1], fun_b[0]);  // AND_Gate
  not not_3 (alu_b, Instr[7]);
  and and_12 (alu_u, Instr[7], ~fun_b[2], ~fun_b[1]);  // AND_Gate
  decoder_2x4 decoder_2x4_3 (.in(cccc[3:2]), .en(ldi_plus), .out({decoder_2x4_3_out, ldi}));
  Pull_Resistor pull_resistor_24 (.node(L_CVZN));
  decoder_2x4 decoder_2x4_4 (.in(cccc[3:2]), .en(and_16_out), .out({ldsp, stsp, po, pu}));
  and and_13 (and_13_out, fun_b[2], fun_b[1], fun_b[0]);
  and and_14 (mem_op, Instr[7], ~fun_b[2], fun_b[1]);  // AND_Gate
  and and_15 (cmp, alu_b, and_13_out);
  decoder_2x4 decoder_2x4_5 (.in(cccc[1:0]), .en(decoder_2x4_3_out[1]), .out({rts, jsr, WAIT, decoder_2x4_5_out[0]}));
  decoder_2x4 decoder_2x4_6 (.in(cccc[1:0]), .en(decoder_2x4_3_out[2]), .out({osix, crc, rti, ioi}));
  decoder_2x4 decoder_2x4_7 (.in(cccc[1:0]), .en(decoder_2x4_3_out[3]), .out(decoder_2x4_7_out));
  PS ps_1 (
    .ldPS(LatchPSR), .CVZN(alu_1_cvzn), .bus_in(data_in), .latch_CVZN(L_CVZN), .bus_out(data_in),
    .\assert (PSR2b1), .Output({PrSt, CVZN}), .Cl(Cl), .Rset(rset));
  and and_16 (and_16_out, Instr[7], fun_b[2], ~fun_b[1], ~fun_b[0]);  // AND_Gate
  and and_17 (and_17_out, Instr[7], fun_b[2], fun_b[1]);
  and and_18 (branch, and_17_out, ~fun_b[0]);  // AND_Gate
  not not_4 (HALT_prime, decoder_2x4_5_out[0]);
  IR ir_1 (.latch(Fetch), .Cl(Cl), .Reset(rset), .Output({Instr[7], fun_b, cccc}), .\input (data_in), .int_req(IAck));
  Register #(.width(3), .trigger("falling")) register_2 (.D(data_in[6:4]), .en(L_Pg), .Q(PgReg), .clk(Cl), .clr(rset));
  Pull_Resistor pull_resistor_25 (.node(PSR2b1));
  Pull_Resistor pull_resistor_26 (.node(LatchPSR));
  and and_19 (ldc, and_17_out, fun_b[0]);
  or or_8 (osi, ioi, osix);
  not not_5 (not_5_out, fun_b[0]);
  _2driver u_2driver_1 (.in_1(pu), .in_2(Ph1), .out_3(SPact));  // open: out_4
  _6driver u_6driver_1 (
    .in_1(pu), .in_2(Ph2), .out_3(SP2b0), .out_4(RdA), .out_5(mem), .out_6(data_code_prime));  // open: out_7, out_8
  _6driver u_6driver_2 (
    .in_1(jsr), .in_2(Ph1), .out_3(SPact), .out_4(PC2b0), .out_5(mem), .out_6(load_st_prime), .out_7(RXL),
    .out_8(PCinc));
  _8driver u_8driver_1 (
    .in_1(rts), .in_2(Ph1), .out_3(SP2b0), .out_4(up_dwn_prime), .out_5(SPact), .out_6(mem),
    .out_7(load_st_prime), .out_8(data_code_prime), .out_9(latchPC));  // open: out_10
  _6driver u_6driver_3 (
    .in_1(osix), .in_2(Ph1), .out_3(SPact), .out_4(PC2b0), .out_5(PCinc), .out_6(load_st_prime), .out_7(mem),
    .out_8(L_Pg));
  _2driver u_2driver_2 (.in_1(ioi), .in_2(Ph1), .out_3(SP2b0));  // open: out_4
  _4driver u_4driver_1 (.in_1(alu_b), .in_2(Ph1), .out_3(RsA), .out_4(RdA), .out_6(L_CVZN));  // open: out_5
  _2driver u_2driver_3 (.in_1(alu_b), .in_2(Ph2), .out_3(Latch), .out_4(RRA));
  and and_20 (and_20_out, mem_op, fun_b[0]);
  and and_21 (and_21_out, mem_op, not_5_out);
  _2driver u_2driver_4 (.in_1(ldsp), .in_2(Ph1), .out_3(SP2b1), .out_4(Latch));
  br_dcsn br_dcsn_1 (.cccc(cccc), .CVZN(CVZN), .go(br_dcsn_1_go));
  not not_6 (not_6_out, br_dcsn_1_go);
  _6driver u_6driver_4 (
    .in_1(crc), .in_2(Ph1), .out_3(SP2b0), .out_4(mem), .out_5(load_st_prime), .out_7(data_code_prime),
    .out_8(RXL));  // open: out_6
  _8driver u_8driver_2 (
    .in_1(rti), .in_2(Ph1), .out_3(SP2b0), .out_4(data_code_prime), .out_5(mem), .out_6(load_st_prime),
    .out_7(SPact), .out_8(up_dwn_prime), .out_10(LatchPSR));  // open: out_9
  _6driver u_6driver_5 (
    .in_1(and_20_out), .in_2(Ph1), .out_3(RsA), .out_4(Latch), .out_5(load_st_prime), .out_6(mem),
    .out_8(data_code_prime));  // open: out_7
  and and_22 (and_22_out, branch, br_dcsn_1_go);
  and and_23 (and_23_out, branch, not_6_out);
  _4driver u_4driver_2 (.in_1(alu_u), .in_2(Ph1), .out_3(RsA), .out_4(Rd_as_src), .out_5(Latch), .out_6(L_CVZN));
  _8driver u_8driver_3 (
    .in_1(po), .in_2(Ph1), .out_3(SP2b0), .out_4(mem), .out_5(load_st_prime), .out_6(Latch), .out_7(SPact),
    .out_8(up_dwn_prime), .out_9(data_code_prime));  // open: out_10
  _2driver u_2driver_5 (.in_1(and_23_out), .in_2(Ph1), .out_3(PCinc));  // open: out_4
  _6driver u_6driver_6 (
    .in_1(jsr), .in_2(Ph2), .out_3(PC2b1), .out_4(SP2b0), .out_5(mem), .out_6(data_code_prime), .out_7(RX2pc));  // open: out_8
  and and_24 (alu_u1, alu_u, Ph1);
  _6driver u_6driver_7 (
    .in_1(and_21_out), .in_2(Ph1), .out_3(RsA), .out_4(RdA), .out_5(mem), .out_6(data_code_prime));  // open: out_7, out_8
  _2driver u_2driver_6 (.in_1(stsp), .in_2(Ph1), .out_3(RdA), .out_4(SPL));
  _4driver u_4driver_3 (
    .in_1(and_22_out), .in_2(Ph1), .out_3(PC2b0), .out_4(mem), .out_5(load_st_prime), .out_6(latchPC));
  _6driver u_6driver_8 (
    .in_1(ldi), .in_2(Ph1), .out_3(PC2b0), .out_4(mem), .out_5(load_st_prime), .out_6(Latch), .out_8(PCinc));  // open: out_7
  _6driver u_6driver_9 (
    .in_1(crc), .in_2(Ph2), .out_3(SP2b0), .out_4(mem), .out_5(PC2b1), .out_6(data_code_prime), .out_7(RX2pc));  // open: out_8
  _6driver u_6driver_10 (
    .in_1(osi), .in_2(Ph2), .out_3(SP2b0), .out_4(data_code_prime), .out_5(mem), .out_6(PC2b1), .out_7(SPact));  // open: out_8
  _4driver u_4driver_4 (.in_1(osi), .in_2(Ph4), .out_3(vec), .out_4(latchPC), .out_5(mem), .out_6(load_st_prime));
  _8driver u_8driver_4 (
    .in_1(rti), .in_2(Ph2), .out_3(SP2b0), .out_4(latchPC), .out_5(mem), .out_6(load_st_prime),
    .out_7(SPact), .out_8(up_dwn_prime), .out_9(data_code_prime));  // open: out_10
  _4driver u_4driver_5 (.in_1(ldc), .in_2(Ph1), .out_3(RsA), .out_4(Latch), .out_5(load_st_prime), .out_6(mem));
  _4driver u_4driver_6 (.in_1(osi), .in_2(Ph3), .out_3(SP2b0), .out_4(mem), .out_5(data_code_prime), .out_6(PSR2b1));
  _6driver u_6driver_11 (
    .in_1(osi), .in_2(Ph5), .out_3(vec), .out_4(odd), .out_5(load_st_prime), .out_6(mem), .out_8(LatchPSR));  // open: out_7

  assign data_out = data_in;

  // Other names for the same wires on the sheet: fun_u[2:0] = {fun_b[0], cccc[3:2]}; Instr[6:0] = {fun_b, cccc};
  //   ldi_op[3:0] = cccc; Rs[1:0] = cccc[3:2]; data = data_code_prime; l_st_prime = fun_b[0]; int = IAck;
  //   ld = load_st_prime; Rd[1:0] = cccc[1:0]; vec_adr[0] = odd

  // Notes on the sheet:
  //   IRQ: pull=down
  //   wait logic
  //   Temporary page select for ioi/osix
  //   extrn. vector
  //   Interrupt logic
  //   Sequencer
  //   extended cycles (>4)
  //   int. granted
  //   buffer_1 drives only 1 and floats otherwise
  //   buffer_2 drives only 1 and floats otherwise
  //   buffer_3 drives only 1 and floats otherwise
  //   buffer_4 drives only 1 and floats otherwise
  //   hold vec
  //   Primary decoder
  //   ldi+ Primary decoder
  //   Coco-de-Mer-8 (Mark 3, 2016)
  //   ALU 2-op
  //   osix
  //   ioi
  //   rti
  //   ld/st/ldc
  //   push
  //   the rest of the phases as osix
  //   ldsp
  //   jsr
  //   Secondary Decoder
  //   ALU 1-op
  //   rts
  //   crc
  //   stsp
  //   pop
  //   br
  //   ldi
endmodule

module Reg (
  input  asrt0,
  input  [7:0] \input ,
  input  latch,
  input  asrt1,
  input  Cl,
  input  Reset,
  output [7:0] mon,
  output [7:0] out0,
  output [7:0] out1
);

  wire not_1_out;
  wire [7:0] register_1_q;

  Register #(.trigger("high")) register_1 (.D(\input ), .en(latch), .Q(register_1_q), .clk(Cl), .clr(Reset));
  Register #(.trigger("high")) register_2 (.D(register_1_q), .en(1'b1), .Q(mon), .clk(not_1_out), .clr(Reset));
  not not_1 (not_1_out, Cl);
  assign out0 = asrt0 ? mon : 8'bz;  // Controlled_Buffer controlled_buffer_1
  assign out1 = asrt1 ? mon : 8'bz;  // Controlled_Buffer controlled_buffer_2

  // Notes on the sheet:
  //   input: pull=down
  //   Note: the library component "register" above
  //   is a replacement of 8D-latch and functions  identifcally
endmodule

// mux2
module _8mux2x1 (
  input  [7:0] in0,
  input  select,
  input  [7:0] in1,
  output [7:0] out
);

  wire [7:0] and_1_out, and_2_out;
  wire [7:7] not_1_out;

  not not_1 (not_1_out[7], select);
  assign and_1_out = in0 & {8{not_1_out[7]}};  // AND_Gate and_1, 8 bits wide
  assign and_2_out = {8{select}} & in1;  // AND_Gate and_2, 8 bits wide
  assign out = and_1_out | and_2_out;  // OR_Gate or_1, 8 bits wide

  // Notes on the sheet:
  //   in0: pull=down
  //   in1: pull=down
endmodule

module PC (
  input  asrt0,
  input  inc,
  input  [7:0] \input ,
  input  latch,
  input  asrt1,
  input  Cl,
  input  Reset,
  output [7:0] mon,
  output [7:0] out0,
  output [7:0] out1
);

  wire not_1_out, or_1_out;
  wire [7:0] controlled_buffer_1_out, n8adder_1_sum, register_1_q;

  _8adder u_8adder_1 (.op1(mon), .Cin(1'b1), .op2({8{1'b0}}), .sum(n8adder_1_sum));  // open: Cout
  assign controlled_buffer_1_out = inc ? n8adder_1_sum : 8'bz;  // Controlled_Buffer controlled_buffer_1
  assign controlled_buffer_1_out = latch ? \input  : 8'bz;  // Controlled_Buffer controlled_buffer_2
  or or_1 (or_1_out, inc, latch);
  Register #(.trigger("high")) register_1 (
    .D(controlled_buffer_1_out), .en(or_1_out), .Q(register_1_q), .clk(Cl), .clr(Reset));
  not not_1 (not_1_out, Cl);
  Register #(.trigger("high")) register_2 (.D(register_1_q), .en(1'b1), .Q(mon), .clk(not_1_out), .clr(Reset));
  assign out0 = asrt0 ? mon : 8'bz;  // Controlled_Buffer controlled_buffer_3
  assign out1 = asrt1 ? mon : 8'bz;  // Controlled_Buffer controlled_buffer_4

  // Notes on the sheet:
  //   input: pull=down
  //   Q
endmodule

module SP (
  input  up_down_prime,
  input  asrt0,
  input  step,
  input  [7:0] \input ,
  input  latch,
  input  asrt1,
  input  Cl,
  input  Reset,
  output [7:0] out0,
  output [7:0] out1,
  output [7:0] mon
);

  wire not_2_out, or_1_out;
  wire [7:0] controlled_buffer_1_out, n8adder_1_sum, register_1_q;
  wire [7:7] not_1_out;

  assign controlled_buffer_1_out = step ? n8adder_1_sum : 8'bz;  // Controlled_Buffer controlled_buffer_1
  assign controlled_buffer_1_out = latch ? \input  : 8'bz;  // Controlled_Buffer controlled_buffer_2
  not not_1 (not_1_out[7], up_down_prime);
  Register #(.trigger("high")) register_1 (
    .D(controlled_buffer_1_out), .en(or_1_out), .Q(register_1_q), .clk(Cl), .clr(Reset));
  or or_1 (or_1_out, step, latch);
  Register #(.trigger("high")) register_2 (.D(register_1_q), .en(1'b1), .Q(mon), .clk(not_2_out), .clr(Reset));
  not not_2 (not_2_out, Cl);
  _8adder u_8adder_1 (.op1({{7{not_1_out[7]}}, 1'b1}), .Cin(1'b0), .op2(mon), .sum(n8adder_1_sum));  // open: Cout
  assign out0 = asrt0 ? mon : 8'bz;  // Controlled_Buffer controlled_buffer_3
  assign out1 = asrt1 ? mon : 8'bz;  // Controlled_Buffer controlled_buffer_4

  // Notes on the sheet:
  //   input: pull=down
endmodule

// Register File
module regfile (
  input  [1:0] RsSel,
  input  RsAssert,
  input  UseRd_Rs_prime,
  input  [1:0] RdSel,
  input  RdAssert,
  input  latch,
  input  [7:0] Bus1,
  input  [7:0] ALUres,
  input  latchPC,
  input  latchSP,
  input  Cl,
  input  rset,
  input  RR2bus1,
  input  latchRX,
  input  rx2pc_b12pc_prime,
  input  PC2bus0,
  input  SPact,
  input  SP2bus1,
  input  SP2bus0,
  input  PCinc,
  input  PC2bus1,
  input  up_down_prime,
  output [7:0] R0,
  output [7:0] Bus0o,
  output [7:0] R1,
  output [7:0] R2,
  output [7:0] R3,
  output [7:0] PC,
  output [7:0] SP,
  output [7:0] Bus1o
);

  wire not_1_out, not_2_out, or_1_out, or_2_out;
  wire [1:0] n2mux2x1_1_out;
  wire [3:0] decoder_2x4_1_out, decoder_2x4_2_out, decoder_2x4_3_out;
  wire [7:0] controlled_buffer_1_out, n8mux2x1_1_out, RX_out0;

  not not_1 (not_1_out, UseRd_Rs_prime);
  decoder_2x4 decoder_2x4_1 (.in(n2mux2x1_1_out), .en(RsAssert), .out(decoder_2x4_1_out));
  _2mux2x1 u_2mux2x1_1 (.in0(RdSel), .select(not_1_out), .in1(RsSel), .out(n2mux2x1_1_out));
  decoder_2x4 decoder_2x4_2 (.in(RdSel), .en(RdAssert), .out(decoder_2x4_2_out));
  decoder_2x4 decoder_2x4_3 (.in(RdSel), .en(latch), .out(decoder_2x4_3_out));
  assign controlled_buffer_1_out = not_2_out ? Bus1 : 8'bz;  // Controlled_Buffer controlled_buffer_1
  Reg u_R0 (
    .asrt0(decoder_2x4_1_out[0]), .out0(Bus0o), .\input (controlled_buffer_1_out),
    .latch(decoder_2x4_3_out[0]), .out1(controlled_buffer_1_out), .asrt1(decoder_2x4_2_out[0]), .Cl(Cl),
    .Reset(rset), .mon(R0));
  or or_1 (or_1_out, RdAssert, PC2bus1, SP2bus1);
  not not_2 (not_2_out, or_1_out);
  Reg u_R1 (
    .asrt0(decoder_2x4_1_out[1]), .out0(Bus0o), .\input (controlled_buffer_1_out),
    .latch(decoder_2x4_3_out[1]), .out1(controlled_buffer_1_out), .asrt1(decoder_2x4_2_out[1]), .Cl(Cl),
    .Reset(rset), .mon(R1));
  Reg u_R2 (
    .asrt0(decoder_2x4_1_out[2]), .out0(Bus0o), .\input (controlled_buffer_1_out),
    .latch(decoder_2x4_3_out[2]), .out1(controlled_buffer_1_out), .asrt1(decoder_2x4_2_out[2]), .Cl(Cl),
    .Reset(rset), .mon(R2));
  Reg u_R3 (
    .asrt0(decoder_2x4_1_out[3]), .out0(Bus0o), .\input (controlled_buffer_1_out),
    .latch(decoder_2x4_3_out[3]), .out1(controlled_buffer_1_out), .asrt1(decoder_2x4_2_out[3]), .Cl(Cl),
    .Reset(rset), .mon(R3));
  Reg RR (
    .asrt0(1'b0), .\input (ALUres), .latch(1'b1), .out1(controlled_buffer_1_out), .asrt1(RR2bus1), .Cl(Cl),
    .Reset(rset));  // open: out0, mon
  Reg RX (
    .asrt0(rx2pc_b12pc_prime), .out0(RX_out0), .\input (controlled_buffer_1_out), .latch(latchRX),
    .asrt1(1'b0), .Cl(Cl), .Reset(rset));  // open: out1, mon
  _8mux2x1 u_8mux2x1_1 (.in0(controlled_buffer_1_out), .select(rx2pc_b12pc_prime), .in1(RX_out0), .out(n8mux2x1_1_out));
  or or_2 (or_2_out, rx2pc_b12pc_prime, latchPC);
  PC pc_1 (
    .inc(PCinc), .latch(or_2_out), .asrt0(PC2bus0), .out0(Bus0o), .out1(controlled_buffer_1_out),
    .asrt1(PC2bus1), .Cl(Cl), .\input (n8mux2x1_1_out), .Reset(rset), .mon(PC));
  SP sp_1 (
    .up_down_prime(up_down_prime), .step(SPact), .\input (controlled_buffer_1_out), .latch(latchSP),
    .asrt0(SP2bus0), .out0(Bus0o), .out1(controlled_buffer_1_out), .asrt1(SP2bus1), .mon(SP), .Cl(Cl),
    .Reset(rset));
  assign Bus1o = or_1_out ? controlled_buffer_1_out : 8'bz;  // Controlled_Buffer controlled_buffer_2

  // Other names for the same wires on the sheet: pc2b1 = PC2bus1; RdA = RdAssert; sp2b1 = SP2bus1

  // Notes on the sheet:
  //   ALUres: pull=down
  //   PCinc: pull=down
endmodule

// 2x4
module decoder_2x4 (
  input  [1:0] in,
  input  en,
  output [3:0] out
);

  wire not_1_out, not_2_out, not_3_out, not_4_out;

  not not_1 (not_1_out, in[1]);
  not not_2 (not_2_out, in[0]);
  not not_3 (not_3_out, in[1]);
  not not_4 (not_4_out, in[0]);
  and and_1 (out[0], not_1_out, en, not_2_out);
  and and_2 (out[1], not_3_out, en, in[0]);
  and and_3 (out[2], in[1], en, not_4_out);
  and and_4 (out[3], in[1], en, in[0]);
endmodule

// mux2x1
module _2mux2x1 (
  input  [1:0] in0,
  input  select,
  input  [1:0] in1,
  output [1:0] out
);

  wire [1:0] and_1_out, and_2_out;
  wire [1:1] not_1_out;

  not not_1 (not_1_out[1], select);
  assign and_1_out = in0 & {2{not_1_out[1]}};  // AND_Gate and_1, 2 bits wide
  assign and_2_out = {2{select}} & in1;  // AND_Gate and_2, 2 bits wide
  assign out = and_1_out | and_2_out;  // OR_Gate or_1, 2 bits wide
endmodule

module ALU (
  input  [2:0] fun,
  input  u_b_prime,
  input  C,
  input  [7:0] X,
  input  [7:0] Y,
  output [3:0] CVZN,
  output [7:0] R
);

  wire add, addc, and_2_out, and_3_out, and_4_out, and_5_out, and_6_out, and_9_out, and_10_out, arith, cmp,
       dec, inc, \logic , move, n8adder_1_cout, neg, \not , not_1_out, not_2_out, not_3_out, not_4_out,
       not_5_out, or_5_out, or_6_out, shift, sub, xor_1_out, xor_4_out, xor_5_out;
  wire [0:0] and_1_out;
  wire [2:0] decoder_2x4_1_out;
  wire [7:0] bin_logic_1_result, controlled_buffer_6_out, n8adder_1_sum, n8mux2x1_1_out, xor_2_out, xor_3_out;
  wire [7:7] or_1_out, or_3_out, or_4_out;

  and and_1 (and_1_out[0], X[7], fun[1]);
  and and_2 (and_2_out, X[7], fun[1]);
  not not_1 (not_1_out, fun[1]);
  and and_3 (and_3_out, not_1_out, C);
  decoder_2x4 decoder_2x4_1 (.in({u_b_prime, fun[2]}), .en(1'b1), .out({shift, decoder_2x4_1_out}));
  or or_1 (or_1_out[7], and_2_out, and_3_out);
  xor xor_1 (xor_1_out, X[6], X[7]);
  not not_2 (not_2_out, fun[1]);
  or or_2 (arith, decoder_2x4_1_out[2], decoder_2x4_1_out[0], cmp);
  and and_4 (and_4_out, xor_1_out, fun[0], not_2_out);
  decoder_2x4 decoder_2x4_2 (.in(fun[1:0]), .en(decoder_2x4_1_out[0]), .out({sub, addc, add, move}));
  decoder_2x4 decoder_2x4_3 (.in(fun[1:0]), .en(decoder_2x4_1_out[2]), .out({inc, dec, neg, \not }));
  _8mux2x1 u_8mux2x1_1 (
    .in0({or_1_out[7], X[7:1]}), .select(fun[0]), .in1({X[6:0], and_1_out[0]}), .out(n8mux2x1_1_out));
  assign CVZN[2] = shift ? and_4_out : 1'bz;  // Controlled_Buffer controlled_buffer_1
  assign {CVZN[0], R[6:0]} = shift ? n8mux2x1_1_out : 8'bz;  // Controlled_Buffer controlled_buffer_2
  and and_5 (and_5_out, not_3_out, shift);
  not not_3 (not_3_out, fun[0]);
  assign CVZN[3] = and_5_out ? X[0] : 1'bz;  // Controlled_Buffer controlled_buffer_3
  assign CVZN[3] = and_6_out ? X[7] : 1'bz;  // Controlled_Buffer controlled_buffer_4
  and and_6 (and_6_out, fun[0], shift);
  not not_4 (not_4_out, cmp);
  and and_7 (cmp, fun[0], fun[1], decoder_2x4_1_out[1]);
  and and_8 (\logic , decoder_2x4_1_out[1], not_4_out);
  bin_logic bin_logic_1 (.op1(X), .op2(Y), .or_and_prime(fun[0]), .xor_and_prime(fun[1]), .result(bin_logic_1_result));
  assign {CVZN[0], R[6:0]} = \logic  ? bin_logic_1_result : 8'bz;  // Controlled_Buffer controlled_buffer_5
  or or_3 (or_3_out[7], cmp, sub);
  or or_4 (or_4_out[7], \not , neg);
  and and_9 (and_9_out, C, addc);
  or or_5 (or_5_out, or_3_out[7], addc, add);
  assign xor_2_out = Y ^ {8{or_3_out[7]}};  // XOR_Gate xor_2, 8 bits wide
  assign xor_3_out = X ^ {8{or_4_out[7]}};  // XOR_Gate xor_3, 8 bits wide
  or or_6 (or_6_out, neg, and_9_out, or_3_out[7]);
  assign controlled_buffer_6_out = or_5_out ? xor_2_out : 8'bz;  // Controlled_Buffer controlled_buffer_6
  nor nor_1 (CVZN[1], R[0], R[1], R[2], R[3], R[4], R[5], R[6], CVZN[0]);
  Pull_Resistor pull_resistor_1 (.node(CVZN[3]));
  Pull_Resistor pull_resistor_2 (.node(CVZN[2]));
  _8adder u_8adder_1 (
    .op1(xor_3_out), .Cin(or_6_out), .op2(controlled_buffer_6_out), .sum(n8adder_1_sum), .Cout(n8adder_1_cout));
  assign controlled_buffer_6_out = inc ? 8'h1 : 8'bz;  // Controlled_Buffer controlled_buffer_7
  assign {CVZN[0], R[6:0]} = arith ? n8adder_1_sum : 8'bz;  // Controlled_Buffer controlled_buffer_8
  assign CVZN[3] = arith ? n8adder_1_cout : 1'bz;  // Controlled_Buffer controlled_buffer_9
  assign controlled_buffer_6_out = dec ? {8{1'b1}} : 8'bz;  // Controlled_Buffer controlled_buffer_10
  Pull_Resistor pull_resistor_3 (.node(controlled_buffer_6_out));
  xor xor_4 (xor_4_out, controlled_buffer_6_out[7], xor_3_out[7]);
  not not_5 (not_5_out, xor_4_out);
  and and_10 (and_10_out, not_5_out, xor_5_out);
  assign CVZN[2] = arith ? and_10_out : 1'bz;  // Controlled_Buffer controlled_buffer_11
  xor xor_5 (xor_5_out, xor_3_out[7], n8adder_1_sum[7]);

  assign R[7] = CVZN[0];

  // Other names for the same wires on the sheet: Snew = X[6]; S = X[7]; V = CVZN[2]; Cout = CVZN[3];
  //   logop[1:0] = fun[1:0]; low[1:0] = fun[1:0]; J = X[0]

  // Notes on the sheet:
  //   Y: pull=down
  //   X: pull=down
  //   R: pull=down
  //   Decoder
  //   if shr then C
  //   Shifts
  //   elseif shra then X7
  //   Binary logic ops
  //   Binary and unary arithmetic ops
  //   Condition codes
  //   Pins
endmodule

// &VX
module bin_logic (
  input  [7:0] op1,
  input  [7:0] op2,
  input  or_and_prime,
  input  xor_and_prime,
  output [7:0] result
);

  wire [7:0] and_1_out, and_2_out, and_3_out, and_4_out, and_5_out, or_1_out, xor_1_out;
  wire [7:7] not_1_out;

  not not_1 (not_1_out[7], xor_and_prime);
  assign xor_1_out = op1 ^ op2;  // XOR_Gate xor_1, 8 bits wide
  assign and_1_out = xor_1_out & {8{xor_and_prime}};  // AND_Gate and_1, 8 bits wide
  assign and_2_out = op1 & op2;  // AND_Gate and_2, 8 bits wide
  assign and_3_out = op1 & {8{or_and_prime}};  // AND_Gate and_3, 8 bits wide
  assign and_4_out = op2 & {8{or_and_prime}};  // AND_Gate and_4, 8 bits wide
  assign or_1_out = and_2_out | and_3_out | and_4_out;  // OR_Gate or_1, 8 bits wide
  assign and_5_out = or_1_out & {8{not_1_out[7]}};  // AND_Gate and_5, 8 bits wide
  assign result = and_5_out | and_1_out;  // OR_Gate or_2, 8 bits wide
endmodule

// 8+
module _8adder (
  input  [7:0] op1,
  input  Cin,
  input  [7:0] op2,
  output [7:0] sum,
  output Cout
);

  wire [6:0] or_1_out;
  wire [7:0] and_1_out, and_2_out, xor_1_out;

  assign xor_1_out = op1 ^ op2;  // XOR_Gate xor_1, 8 bits wide
  assign and_1_out = op1 & op2;  // AND_Gate and_1, 8 bits wide
  assign sum = xor_1_out ^ {or_1_out, Cin};  // XOR_Gate xor_2, 8 bits wide
  assign and_2_out = xor_1_out & {or_1_out, Cin};  // AND_Gate and_2, 8 bits wide
  assign {Cout, or_1_out} = and_2_out | and_1_out;  // OR_Gate or_1, 8 bits wide
endmodule

module IR (
  input  [7:0] \input ,
  input  latch,
  input  int_req,
  input  Cl,
  input  Reset,
  output [7:0] Output
);

  wire not_1_out;
  wire [7:0] n8mux2x1_1_out, register_1_q;

  _8mux2x1 u_8mux2x1_1 (.in0(\input ), .select(int_req), .in1(8'hd8), .out(n8mux2x1_1_out));
  Register #(.trigger("high")) register_1 (.D(n8mux2x1_1_out), .en(latch), .Q(register_1_q), .clk(Cl), .clr(Reset));
  Register #(.trigger("high")) register_2 (.D(register_1_q), .en(1'b1), .Q(Output), .clk(not_1_out), .clr(Reset));
  not not_1 (not_1_out, Cl);

  // Notes on the sheet:
  //   input: pull=down
  //   interrupt instr. op-code
endmodule

// phase
module phase_cntr (
  input  restart,
  input  Cl,
  input  Reset,
  input  hold,
  output [2:0] phase
);

  wire hfad_1_cout, hfad_2_cout, not_2_out, not_3_out;
  wire [2:0] and_1_out, hfad_1_dout, register_1_q;
  wire [2:2] not_1_out;

  not not_1 (not_1_out[2], restart);
  assign and_1_out = hfad_1_dout & {3{not_1_out[2]}};  // AND_Gate and_1, 3 bits wide
  not not_2 (not_2_out, hold);
  Register #(.width(3), .trigger("high")) register_1 (
    .D(and_1_out), .en(not_2_out), .Q(register_1_q), .clk(Cl), .clr(Reset));
  Register #(.width(3), .trigger("high")) register_2 (
    .D(register_1_q), .en(1'b1), .Q(phase), .clk(not_3_out), .clr(Reset));
  not not_3 (not_3_out, Cl);
  hfad hfad_1 (.cin(1'b1), .d(phase[0]), .dout(hfad_1_dout[0]), .cout(hfad_1_cout));
  hfad hfad_2 (.cin(hfad_1_cout), .d(phase[1]), .dout(hfad_1_dout[1]), .cout(hfad_2_cout));
  hfad hfad_3 (.cin(hfad_2_cout), .d(phase[2]), .dout(hfad_1_dout[2]));  // open: cout
endmodule

// mux2x1
module _3mux2x1 (
  input  [2:0] in0,
  input  select,
  input  [2:0] in1,
  output [2:0] out
);

  wire [2:0] and_1_out, and_2_out;
  wire [2:2] not_1_out;

  not not_1 (not_1_out[2], select);
  assign and_1_out = in0 & {3{not_1_out[2]}};  // AND_Gate and_1, 3 bits wide
  assign and_2_out = {3{select}} & in1;  // AND_Gate and_2, 3 bits wide
  assign out = and_1_out | and_2_out;  // OR_Gate or_1, 3 bits wide
endmodule

module PS (
  input  ldPS,
  input  [3:0] CVZN,
  input  [7:0] bus_in,
  input  latch_CVZN,
  input  \assert ,
  input  Cl,
  input  Rset,
  output [7:0] bus_out,
  output [7:0] Output
);

  wire not_1_out, not_2_out, or_1_out;
  wire [3:0] controlled_buffer_1_out, controlled_buffer_2_out, register_2_q, register_3_q;

  assign controlled_buffer_1_out = latch_CVZN ? CVZN : 4'bz;  // Controlled_Buffer controlled_buffer_1
  or or_1 (or_1_out, latch_CVZN, ldPS);
  Register #(.width(4), .trigger("high")) register_1 (
    .D(register_2_q), .en(1'b1), .Q(Output[3:0]), .clk(not_1_out), .clr(Rset));
  Register #(.width(4), .trigger("high")) register_2 (
    .D(controlled_buffer_1_out), .en(or_1_out), .Q(register_2_q), .clk(Cl), .clr(Rset));
  not not_1 (not_1_out, Cl);
  Register #(.width(4), .trigger("high")) register_3 (
    .D(controlled_buffer_2_out), .en(ldPS), .Q(register_3_q), .clk(Cl), .clr(Rset));
  Register #(.width(4), .trigger("high")) register_4 (
    .D(register_3_q), .en(1'b1), .Q(Output[7:4]), .clk(not_2_out), .clr(Rset));
  not not_2 (not_2_out, Cl);
  assign {controlled_buffer_2_out, controlled_buffer_1_out} = ldPS ? bus_in : 8'bz;  // Controlled_Buffer controlled_buffer_2
  assign bus_out = \assert  ? Output : 8'bz;  // Controlled_Buffer controlled_buffer_3

  // Other names for the same wires on the sheet: bus[7:0] = bus_in

  // Notes on the sheet:
  //   latch_CVZN: pull=down
  //   CVZN: pull=down
endmodule

// demux
module _8demux1x2 (
  input  [7:0] in,
  input  sel,
  output [7:0] out1,
  output [7:0] out0
);

  wire not_1_out;

  assign out1 = sel ? in : 8'bz;  // Controlled_Buffer controlled_buffer_1
  not not_1 (not_1_out, sel);
  assign out0 = not_1_out ? in : 8'bz;  // Controlled_Buffer controlled_buffer_2
endmodule

// 3S&
module _4driver (
  input  in_1,
  input  in_2,
  output out_3,
  output out_4,
  output out_5,
  output out_6
);

  and and_1 (out_3, in_2, in_1);
  and and_2 (out_4, in_2, in_1);
  and and_3 (out_5, in_2, in_1);
  and and_4 (out_6, in_2, in_1);

  // Notes on the sheet:
  //   and_1 drives only 1 and floats otherwise
  //   and_2 drives only 1 and floats otherwise
  //   and_3 drives only 1 and floats otherwise
  //   and_4 drives only 1 and floats otherwise
endmodule

// 3S&
module _2driver (
  input  in_1,
  input  in_2,
  output out_3,
  output out_4
);

  and and_1 (out_3, in_2, in_1);
  and and_2 (out_4, in_2, in_1);

  // Notes on the sheet:
  //   and_1 drives only 1 and floats otherwise
  //   and_2 drives only 1 and floats otherwise
endmodule

// 3S&
module _6driver (
  input  in_1,
  input  in_2,
  output out_3,
  output out_4,
  output out_5,
  output out_6,
  output out_7,
  output out_8
);

  and and_1 (out_3, in_2, in_1);
  and and_2 (out_4, in_2, in_1);
  and and_3 (out_6, in_2, in_1);
  and and_4 (out_5, in_2, in_1);
  and and_5 (out_7, in_2, in_1);
  and and_6 (out_8, in_2, in_1);

  // Notes on the sheet:
  //   and_1 drives only 1 and floats otherwise
  //   and_2 drives only 1 and floats otherwise
  //   and_3 drives only 1 and floats otherwise
  //   and_4 drives only 1 and floats otherwise
  //   and_5 drives only 1 and floats otherwise
  //   and_6 drives only 1 and floats otherwise
endmodule

// 3S&
module _8driver (
  input  in_1,
  input  in_2,
  output out_3,
  output out_4,
  output out_5,
  output out_6,
  output out_7,
  output out_8,
  output out_9,
  output out_10
);

  and and_1 (out_3, in_2, in_1);
  and and_2 (out_4, in_2, in_1);
  and and_3 (out_5, in_2, in_1);
  and and_4 (out_6, in_2, in_1);
  and and_5 (out_7, in_2, in_1);
  and and_6 (out_9, in_2, in_1);
  and and_7 (out_8, in_2, in_1);
  and and_8 (out_10, in_2, in_1);

  // Notes on the sheet:
  //   and_1 drives only 1 and floats otherwise
  //   and_2 drives only 1 and floats otherwise
  //   and_3 drives only 1 and floats otherwise
  //   and_4 drives only 1 and floats otherwise
  //   and_5 drives only 1 and floats otherwise
  //   and_6 drives only 1 and floats otherwise
  //   and_7 drives only 1 and floats otherwise
  //   and_8 drives only 1 and floats otherwise
endmodule

module br_dcsn (
  input  [3:0] cccc,
  input  [3:0] CVZN,
  output go
);

  wire and_1_out, and_2_out, and_3_out, and_4_out, and_5_out, and_6_out, and_7_out, not_1_out, not_2_out,
       or_1_out, xnor_1_out;
  wire [3:0] decoder_2x4_1_out, decoder_2x4_2_out;

  not not_1 (not_1_out, cccc[3]);
  decoder_2x4 decoder_2x4_1 (.in(cccc[2:1]), .en(not_1_out), .out(decoder_2x4_1_out));
  decoder_2x4 decoder_2x4_2 (.in(cccc[2:1]), .en(cccc[3]), .out(decoder_2x4_2_out));
  and and_1 (and_1_out, decoder_2x4_1_out[0], CVZN[1]);
  and and_2 (and_2_out, decoder_2x4_1_out[1], CVZN[3]);
  and and_3 (and_3_out, decoder_2x4_1_out[2], CVZN[0]);
  and and_4 (and_4_out, decoder_2x4_1_out[3], CVZN[2]);
  not not_2 (not_2_out, CVZN[1]);
  xnor xnor_1 (xnor_1_out, CVZN[0], CVZN[2]);
  and and_5 (and_5_out, decoder_2x4_2_out[0], not_2_out, CVZN[3]);
  and and_6 (and_6_out, xnor_1_out, decoder_2x4_2_out[1]);
  and and_7 (and_7_out, not_2_out, xnor_1_out, decoder_2x4_2_out[2]);
  or or_1 (or_1_out, and_1_out, and_2_out, and_3_out, and_4_out, and_5_out, and_6_out, and_7_out, decoder_2x4_2_out[3]);
  xor xor_1 (go, cccc[0], or_1_out);

  // Notes on the sheet:
  //   N
  //   Z
  //   V
  //   C
  //   EQ
  //   HS/CS
  //   MI
  //   VS
  //   N=V
  //   Z'
  //   HI
  //   GE
  //   GT
  //   <always>
endmodule

module trap (
  input  up_H,
  input  up_L,
  input  rset,
  input  [7:0] PC,
  input  en,
  output [3:0] H,
  output [3:0] L,
  output trap,
  output en_out
);

  wire nor_1_out, or_1_out, t_ff_1_qn;
  wire [7:0] xor_1_out;

  Counter #(.width(4), .max('hf)) counter_1 (.count(up_H), .Q(H), .clk(up_H));  // open: load, D, carry, clr
  Counter #(.width(4), .max('hf)) counter_2 (.count(up_L), .Q(L), .clk(up_L));  // open: load, D, carry, clr
  or or_1 (or_1_out, rset, t_ff_1_qn);
  assign xor_1_out = {H, L} ^ PC;  // XOR_Gate xor_1, 8 bits wide
  nor nor_1 (nor_1_out, or_1_out, xor_1_out[0], xor_1_out[1], xor_1_out[2], xor_1_out[3], xor_1_out[4], xor_1_out[5], xor_1_out[6], xor_1_out[7]);
  S_R_Flip_Flop #(.trigger("high")) s_r_ff_1 (
    .S(or_1_out), .clk(1'b1), .R(nor_1_out), .Q(trap));  // open: Qn, preset, reset, en
  T_Flip_Flop t_ff_1 (.clk(en), .T(en), .Q(en_out), .Qn(t_ff_1_qn));  // open: preset, reset, en
endmodule

module _8D_latch (
  input  [7:0] data,
  input  clear,
  input  en,
  input  Cl,
  output [7:0] out
);

  wire and_2_out;
  wire [7:0] and_1_out, and_3_out, and_4_out, nor_1_out, not_2_out;
  wire [7:7] not_1_out, or_1_out;

  Pull_Resistor pull_resistor_1 (.node(clear));
  not not_1 (not_1_out[7], clear);
  assign and_1_out = data & {8{not_1_out[7]}};  // AND_Gate and_1, 8 bits wide
  and and_2 (and_2_out, en, Cl);
  assign not_2_out = ~and_1_out;  // NOT_Gate not_2, 8 bits wide
  or or_1 (or_1_out[7], clear, and_2_out);
  assign and_3_out = and_1_out & {8{or_1_out[7]}};  // AND_Gate and_3, 8 bits wide
  assign and_4_out = not_2_out & {8{or_1_out[7]}};  // AND_Gate and_4, 8 bits wide
  assign nor_1_out = ~(and_3_out | out);  // NOR_Gate nor_1, 8 bits wide
  assign out = ~(nor_1_out | and_4_out);  // NOR_Gate nor_2, 8 bits wide
endmodule

// RS
module RS_latch (
  input  S,
  input  R,
  output Q,
  output Q_prime
);

  S_R_Flip_Flop #(.trigger("high")) s_r_ff_1 (
    .S(S), .clk(1'b1), .R(R), .Q(Q), .Qn(Q_prime));  // open: preset, reset, en
endmodule

// +/2
module hfad (
  input  cin,
  input  d,
  output dout,
  output cout
);

  xor xor_1 (dout, cin, d);
  and and_1 (cout, cin, d);
endmodule

module reg_vec (
  input  [2:0] \input ,
  input  latch,
  input  Cl,
  input  Reset,
  output [2:0] mon
);

  wire not_1_out;
  wire [2:0] register_1_q;

  Register #(.width(3), .trigger("high")) register_1 (.D(\input ), .en(latch), .Q(register_1_q), .clk(Cl), .clr(Reset));
  Register #(.width(3), .trigger("high")) register_2 (
    .D(register_1_q), .en(1'b1), .Q(mon), .clk(not_1_out), .clr(Reset));
  not not_1 (not_1_out, Cl);

  // Notes on the sheet:
  //   input: pull=down
endmodule

module system_board (
);

  wire ACK, and_3_out, and_4_out, and_5_out, and_6_out, and_7_out, and_8_out, button_2_out, Cl,
       data_code_prime, Debug_Clear_out, decoder_1_out0, decoder_1_out1, decoder_1_out2, decoder_1_out3,
       decoder_2_out0, decoder_2_out1, decoder_2_out2, decoder_2_out3, decoder_2_out4, decoder_2_out5,
       Home_out, I_Osel, In_out_prime, IO_0_2_out, IO_0_3_out, IO_0_4_out, IO_0_5_out, IO_0_out, IRQ,
       Left_out, mem, msel, n4phase_master_1_ackout, n4phase_master_2_irqout, nand_1_out, not_1_out,
       not_2_out, not_3_out, not_4_out, not_5_out, not_6_out, not_7_out, not_8_out, not_9_out, not_10_out,
       not_11_out, or_1_out, priority_encoder_1_p5, priority_encoder_1_p7, priority_encoder_1_p8,
       pull_resistor_4_node, Rset, Run_Stop_out, undriven;
  wire [2:0] page, priority_encoder_1_p3, vector;
  wire [3:0] register_3_q;
  wire [7:0] addr, cdm_8_1_data_out, cdm_8_1_pc, cdm_8_1_r0, cdm_8_1_r1, cdm_8_1_r2, cdm_8_1_r3, cdm_8_1_sp,
       controlled_buffer_1_out, controlled_buffer_8_out, grobotif_1_p2, I_Odat, register_1_q, register_2_q,
       register_4_q, register_5_q, register_6_q, rom_1_data, rom_2_data, rom_3_data, rom_4_data;
  wire [7:4] pull_resistor_1_node;

  and and_1 (I_Osel, not_1_out, Cl, data_code_prime, mem);
  // Probe on cdm_8_1_r0
  Clock clock_1 (.out(Cl));
  not not_1 (not_1_out, nand_1_out);
  and and_2 (msel, nand_1_out, mem);
  ROM rom_1 (.addr(addr), .data(rom_1_data), .sel(decoder_1_out0));
  ROM rom_2 (.addr(addr), .data(rom_2_data), .sel(decoder_1_out1));
  ROM rom_3 (.addr(addr), .data(rom_3_data), .sel(decoder_1_out2));
  ROM rom_4 (.addr(addr), .data(rom_4_data), .sel(decoder_1_out3));
  // Probe on cdm_8_1_r2
  // Probe on cdm_8_1_r1
  // Probe on cdm_8_1_r3
  Button button_1 (.out(Rset));
  nand nand_1 (nand_1_out, addr[4], addr[5], addr[6], addr[7], data_code_prime);
  assign controlled_buffer_1_out = decoder_1_out0 ? rom_1_data : 8'bz;  // Controlled_Buffer controlled_buffer_1
  assign controlled_buffer_1_out = decoder_1_out1 ? rom_2_data : 8'bz;  // Controlled_Buffer controlled_buffer_2
  assign controlled_buffer_1_out = decoder_1_out2 ? rom_3_data : 8'bz;  // Controlled_Buffer controlled_buffer_3
  assign controlled_buffer_1_out = decoder_1_out3 ? rom_4_data : 8'bz;  // Controlled_Buffer controlled_buffer_4
  // Probe on cdm_8_1_sp
  // Probe on cdm_8_1_pc
  // Probe on addr
  CdM_8 cdm_8_1 (
    .data_code_prime(data_code_prime), .R0(cdm_8_1_r0), .R1(cdm_8_1_r1), .mem(mem), .R2(cdm_8_1_r2),
    .load_st_prime(In_out_prime), .R3(cdm_8_1_r3), .addr(addr), .PC(cdm_8_1_pc), .SP(cdm_8_1_sp),
    .data_out(cdm_8_1_data_out), .data_in(controlled_buffer_1_out), .page(page), .IRQ(IRQ), .IAck(ACK),
    .vector(vector), .rset(Rset), .clk(Cl));
  Decoder #(.select(3), .disabled(0)) decoder_1 (
    .out0(decoder_1_out0), .out1(decoder_1_out1), .out2(decoder_1_out2), .out3(decoder_1_out3), .sel(page),
    .en(and_4_out));  // open: out4, out5, out6, out7
  not not_2 (not_2_out, Cl);
  and and_3 (and_3_out, data_code_prime, msel);
  not not_3 (not_3_out, data_code_prime);
  and and_4 (and_4_out, not_3_out, mem);
  RAM ram_1 (.addr(addr), .data(I_Odat), .sel(and_3_out), .clk(not_2_out), .ld(In_out_prime), .clr(button_2_out));
  Button button_2 (.out(button_2_out));
  not not_4 (not_4_out, In_out_prime);
  assign I_Odat = not_4_out ? cdm_8_1_data_out : 8'bz;  // Controlled_Buffer controlled_buffer_5
  assign controlled_buffer_1_out = In_out_prime ? I_Odat : 8'bz;  // Controlled_Buffer controlled_buffer_6
  not not_5 (not_5_out, addr[3]);
  Decoder #(.select(3), .disabled(0)) decoder_2 (
    .out0(decoder_2_out0), .out1(decoder_2_out1), .out2(decoder_2_out2), .out3(decoder_2_out3),
    .out4(decoder_2_out4), .out5(decoder_2_out5), .sel(addr[2:0]), .en(not_5_out));  // open: out6, out7
  and IO_0 (IO_0_out, decoder_2_out2, ~In_out_prime, I_Osel);  // AND_Gate
  and IO_0_2 (IO_0_2_out, decoder_2_out4, In_out_prime, I_Osel);
  assign I_Odat = IO_0_2_out ? {register_6_q[7], 4'b0000, register_6_q[2:0]} : 8'bz;  // Controlled_Buffer controlled_buffer_7
  and and_5 (and_5_out, ~In_out_prime, I_Osel, decoder_2_out0);  // AND_Gate
  not not_6 (not_6_out, not_9_out);
  not not_7 (not_7_out, not_6_out);
  and and_6 (and_6_out, In_out_prime, I_Osel, decoder_2_out0);
  Register register_1 (.D(I_Odat), .Q(register_1_q), .clk(IO_0_out));  // open: en, clr
  not not_8 (not_8_out, and_5_out);
  not not_9 (not_9_out, not_8_out);
  RS_latch rs_latch_1 (.S(not_7_out), .R(not_10_out), .Q(pull_resistor_1_node[7]));  // open: Q_prime
  and IO_0_3 (IO_0_3_out, decoder_2_out1, ~In_out_prime, I_Osel);  // AND_Gate
  Register register_2 (.D(I_Odat), .Q(register_2_q), .clk(IO_0_4_out));  // open: en, clr
  and IO_0_4 (IO_0_4_out, decoder_2_out3, ~In_out_prime, I_Osel);  // AND_Gate
  and IO_0_5 (IO_0_5_out, decoder_2_out5, ~In_out_prime, I_Osel);  // AND_Gate
  // Probe on IO_0_2_out
  _4phase_master u_4phase_master_1 (
    .IRQout(IRQ), .ACKin(ACK), .IRQin(n4phase_master_2_irqout), .ACKout(n4phase_master_1_ackout),
    .vecbus(vector), .rset(Rset), .vec(3'b000), .req(undriven));  // open: ack
  assign controlled_buffer_8_out = and_5_out ? I_Odat : 8'bz;  // Controlled_Buffer controlled_buffer_8
  // Probe on {pull_resistor_1_node, register_3_q}
  Register #(.width(4)) register_3 (
    .D(controlled_buffer_8_out[3:0]), .Q(register_3_q), .clk(not_9_out));  // open: en, clr
  not not_10 (not_10_out, grobotif_1_p2[7]);
  Register register_4 (.D(I_Odat), .Q(register_4_q), .clk(IO_0_3_out));  // open: en, clr
  // Probe on register_5_q
  Register register_5 (.D(I_Odat), .Q(register_5_q), .clk(IO_0_5_out), .clr(Debug_Clear_out));  // open: en
  Button Debug_Clear (.out(Debug_Clear_out));
  Pull_Resistor pull_resistor_1 (.node(pull_resistor_1_node[4]));
  Pull_Resistor pull_resistor_2 (.node(pull_resistor_1_node[5]));
  Pull_Resistor pull_resistor_3 (.node(pull_resistor_1_node[6]));
  Hex_Digit_Display hex_digit_display_1 (.value(register_1_q[7:4]));  // open: dp
  Hex_Digit_Display hex_digit_display_2 (.value(register_1_q[3:0]));  // open: dp
  // Probe on grobotif_1_p2
  // GrobotIF grobotif_1: pin names not known; wires that end beside it: {pull_resistor_1_node, register_3_q}, grobotif_1_p2, In_out_prime, I_Odat, I_Osel, addr[3:0]
  Hex_Digit_Display hex_digit_display_3 (.value(register_2_q[7:4]));  // open: dp
  Button Home (.out(Home_out));
  Button Run_Stop (.out(Run_Stop_out));
  Pull_Resistor #(.pull(1)) pull_resistor_4 (.node(pull_resistor_4_node));
  assign I_Odat = and_6_out ? grobotif_1_p2 : 8'bz;  // Controlled_Buffer controlled_buffer_9
  LED W (.in(register_4_q[2]));
  Hex_Digit_Display hex_digit_display_4 (.value(register_2_q[3:0]));  // open: dp
  Button Left (.out(Left_out));
  // Priority_Encoder #(.disabled(0)) priority_encoder_1: pin names not known; wires that end beside it: pull_resistor_4_node, Run_Stop_out, priority_encoder_1_p3, Home_out, priority_encoder_1_p5, Left_out, priority_encoder_1_p7, priority_encoder_1_p8
  and and_7 (and_7_out, priority_encoder_1_p5, not_11_out);
  or or_1 (or_1_out, and_7_out, and_8_out);
  and and_8 (and_8_out, register_6_q[7], IO_0_2_out);
  LED ER (.in(grobotif_1_p2[6]));
  LED N (.in(register_4_q[1]));
  LED E (.in(register_4_q[0]));
  LED S (.in(register_4_q[3]));
  Button Right (.out(priority_encoder_1_p7));
  Register #(.width(3)) register_6 (
    .D(priority_encoder_1_p3), .Q(register_6_q[2:0]), .clk(priority_encoder_1_p5));  // open: en, clr
  D_Flip_Flop #(.trigger("falling")) d_ff_1 (
    .clk(or_1_out), .D(not_11_out), .Q(register_6_q[7]));  // open: Qn, preset, en, reset
  not not_11 (not_11_out, register_6_q[7]);
  LED F (.in(grobotif_1_p2[2]));
  LED FR (.in(grobotif_1_p2[1]));
  LED FL (.in(grobotif_1_p2[3]));
  LED L (.in(grobotif_1_p2[4]));
  LED X (.in(grobotif_1_p2[5]));
  Button Fwd (.out(priority_encoder_1_p8));
  _4phase_master u_4phase_master_2 (
    .IRQout(n4phase_master_2_irqout), .ACKin(n4phase_master_1_ackout), .IRQin(1'b0), .vecbus(vector),
    .rset(Rset), .vec(3'b001));  // open: ACKout, ack, req
  LED R (.in(grobotif_1_p2[0]));

  // Other names for the same wires on the sheet: I_Oadr[3:0] = addr[3:0]; rd_wr_prime = In_out_prime

  // Notes on the sheet:
  //   instr memory
  //   memory-mapped I/O
  //   contents of rom_1 (hex, n*v repeats v):
  //   d0 f0 c8 d0 f4 b1 5 e5 5 d2 84 76 e1 10 d6 53 d2 87 76 e1 17 d6 6e d2 86 76 e1 1e d6 b1 d2 85 76 e1
  //   25 d6 a0 d2 83 76 e1 2c d6 2f ee 3 d4 d1 0 d6 c5 d2 f4 d3 83 b8 73 e1 3c d7 d3 f5 ad d2 10 46 e1 46
  //   d6 a0 d2 4 46 e1 4f d6 6e ee 51 d6 b1 ee 33 d1 8 d6 c5 d3 0 d2 2 ae d3 f1 ae d3 1 d2 1 ae d3 f2 ae
  //   d3 2 ae d3 f3 ae d7 d1 4 d6 c5 d2 0 ba d3 2 bf d0 2 78 e1 7e 8f d0 8 78 e1 84 8b d0 2 a3 d0 f3 a3 d3
  //   1 bf d0 1 78 e1 93 8f d0 4 78 e1 99 8b d0 1 a3 d0 f2 a3 d7 d1 2 d6 c5 d3 0 bf 2f d2 10 4e e0 af d3 1
  //   ee be d1 1 d6 c5 d3 0 bf 93 f e1 be d3 8 d2 0 ab d2 f1 ab d7 d0 f0 a1 d2 80 b1 46 e0 ca d2 60 46 e0
  //   d6 c6 ee dc d2 1f 49 d0 3 a1 d7
  //   contents of rom_4 (hex, n*v repeats v):
  //   240*0 22 33
  //   Bank 0
  //   Bank 1
  //   Bank 2
  //   Bank 3
  //   data memory
  //   I/O bus
  //   IO sel
  //   IO in/out'
  //   IO data
  //   IO addr decode
  //   interrupt chain
  //   read trigger
  //   write trigger
  //   ExpansionOP
  //   X
  //   Y
  //   Fatal Error
  //   Heading
  //   Button data
  //   status
  //   Status
endmodule

// 4Ph
module _4phase_master (
  input  IRQin,
  input  ACKin,
  input  req,
  input  rset,
  input  [2:0] vec,
  output [2:0] vecbus,
  output IRQout,
  output ACKout,
  output ack
);

  wire and_4_out, and_5_out, and_6_out, and_7_out, and_8_out, and_9_out, not_1_out, not_2_out, not_3_out,
       not_4_out, or_1_out;
  wire [1:0] and_1_out, register_1_q;

  and and_1 (and_1_out[0], ~register_1_q[0], ~register_1_q[1]);  // AND_Gate
  and and_2 (and_1_out[1], register_1_q[0], ~register_1_q[1]);  // AND_Gate
  Register #(.width(2)) register_1 (.D(and_1_out), .en(1'b1), .Q(register_1_q), .clk(or_1_out), .clr(rset));
  or or_1 (or_1_out, and_4_out, and_5_out, and_7_out);
  and and_3 (ack, register_1_q[1], ~register_1_q[0]);  // AND_Gate
  and and_4 (and_4_out, ack, not_1_out);
  not not_1 (not_1_out, ACKin);
  assign vecbus = ack ? vec : 3'bz;  // Controlled_Buffer controlled_buffer_1
  or or_2 (IRQout, and_9_out, not_2_out);
  not not_2 (not_2_out, not_3_out);
  not not_3 (not_3_out, and_6_out);
  and and_5 (and_5_out, and_6_out, ACKin);
  and and_6 (and_6_out, ~register_1_q[1], register_1_q[0]);  // AND_Gate
  and and_7 (and_7_out, and_8_out, req, not_4_out);
  and and_8 (and_8_out, ~register_1_q[1], ~register_1_q[0]);  // AND_Gate
  not not_4 (not_4_out, ACKin);
  and and_9 (and_9_out, IRQin, and_8_out);
  and and_10 (ACKout, and_8_out, ACKin);
endmodule
