// Logisim project gRobotTest.circ as structural Verilog: 1 circuit, main circuit main
module main (
  input  [7:0] in_1,
  output [7:0] out_2
);

  // GrobotIF grobotif_1: pin names not known; wires that end beside it: in_1, out_2

  // Notes on the sheet:
  //   in_1: pull=down
  //   out_2: pull=down
endmodule
