// Logisim project grobotIF_DriverCircuit.circ as structural Verilog: 1 circuit, main circuit main
module main (
  input  [2:0] CtrlTest,
  input  [7:0] TestData
);

  wire and_1_out, and_2_out, not_1_out, not_2_out, not_3_out, not_4_out, not_5_out;
  wire [3:0] register_1_q;
  wire [7:0] controlled_buffer_1_out, grobotif_1_p2;
  wire [7:4] pull_resistor_1_node;

  and and_1 (and_1_out, ~CtrlTest[0], CtrlTest[1], CtrlTest[2]);  // AND_Gate
  not not_1 (not_1_out, not_4_out);
  not not_2 (not_2_out, not_1_out);
  and and_2 (and_2_out, CtrlTest[0], CtrlTest[1], CtrlTest[2]);
  assign controlled_buffer_1_out = and_1_out ? TestData : 8'bz;  // Controlled_Buffer controlled_buffer_1
  not not_3 (not_3_out, and_1_out);
  not not_4 (not_4_out, not_3_out);
  Register #(.width(4)) register_1 (
    .D(controlled_buffer_1_out[3:0]), .Q(register_1_q), .clk(not_4_out));  // open: en, clr
  S_R_Flip_Flop s_r_ff_1 (
    .Q(pull_resistor_1_node[7]), .preset(not_2_out), .reset(not_5_out));  // open: S, clk, R, Qn, en
  not not_5 (not_5_out, grobotif_1_p2[7]);
  // Probe on {pull_resistor_1_node, register_1_q}
  Pull_Resistor pull_resistor_1 (.node(pull_resistor_1_node[4]));
  Pull_Resistor pull_resistor_2 (.node(pull_resistor_1_node[5]));
  Pull_Resistor pull_resistor_3 (.node(pull_resistor_1_node[6]));
  // Probe on grobotif_1_p2
  // GrobotIF grobotif_1: pin names not known; wires that end beside it: {pull_resistor_1_node, register_1_q}, grobotif_1_p2
  assign TestData = and_2_out ? grobotif_1_p2 : 8'bz;  // Controlled_Buffer controlled_buffer_2

  // Other names for the same wires on the sheet: In_out_prime = CtrlTest[0]; I_Osel = CtrlTest[1];
  //   I_Odat[7:0] = TestData

  // Notes on the sheet:
  //   I/O bus
  //   IO addr decode
endmodule
