// Logisim project LogisimTestGRIF.circ as structural Verilog: 1 circuit, main circuit main
module main (
  input  [7:0] in_1,
  output [7:0] out_2
);

  wire button_1_out, button_2_out, button_3_out, or_1_out;

  Button button_1 (.out(button_1_out));
  Button button_2 (.out(button_2_out));
  Button button_3 (.out(button_3_out));
  // GrobotIF grobotif_1: pin names not known; wires that end beside it: button_1_out, in_1, out_2
  or or_1 (or_1_out, out_2[7], button_2_out);
  S_R_Flip_Flop s_r_ff_1 (
    .S(or_1_out), .R(button_3_out), .preset(or_1_out), .reset(button_3_out));  // open: clk, Q, Qn, en

  // Notes on the sheet:
  //   in_1: pull=down
endmodule
