// Logisim project ManCon.circ as structural Verilog: 1 circuit, main circuit main
module main (
);

  wire [7:0] button_3_out, grobotif_1_p2;

  Button button (.out(button_3_out[2]));
  Button button_2 (.out(button_3_out[1]));
  Button I (.out(button_3_out[3]));
  Button button_3 (.out(button_3_out[0]));
  Pull_Resistor pull_resistor_1 (.node(button_3_out[6]));
  or or_1 (button_3_out[7], button_3_out[1], button_3_out[3], button_3_out[2], button_3_out[0]);
  LED ERR (.in(grobotif_1_p2[6]));
  LED RDY (.in(grobotif_1_p2[7]));
  LED CRASH (.in(grobotif_1_p2[5]));
  // GrobotIF grobotif_1: pin names not known; wires that end beside it: {button_3_out[7:6], {2{button_3_out[6]}}, button_3_out[3:0]}, grobotif_1_p2
  DotMatrix #(.matrixrows(1), .dotshape("circle")) dotmatrix_1 (
    .col0(grobotif_1_p2[4]), .col1(grobotif_1_p2[3]), .col2(grobotif_1_p2[2]), .col3(grobotif_1_p2[1]),
    .col4(grobotif_1_p2[0]));
endmodule
