// Logisim project TestGRIF.circ as structural Verilog: 1 circuit, main circuit main
module main (
  input  [6:0] Bit__6_5_4_NC__3_Init_2_Fw_1_Lf_0_Rt_0_Lk,
  output [7:0] Bit__7_Rdy__6_Err_5_Cld__4_0_Look
);

  wire button_1_out, grobotif_1_p3, not_1_out;
  wire [7:7] Act__Bit_7_out;

  Button Act__Bit_7 (.out(Act__Bit_7_out[7]));
  Button button_1 (.out(button_1_out));
  // GrobotIF grobotif_1: pin names not known; wires that end beside it: {Act__Bit_7_out[7], Bit__6_5_4_NC__3_Init_2_Fw_1_Lf_0_Rt_0_Lk}, Bit__7_Rdy__6_Err_5_Cld__4_0_Look, grobotif_1_p3
  not not_1 (not_1_out, Bit__7_Rdy__6_Err_5_Cld__4_0_Look[7]);
  D_Flip_Flop d_ff_1 (.clk(grobotif_1_p3), .preset(not_1_out), .reset(button_1_out));  // open: D, Q, Qn, en
endmodule
